# Fritzing sketch Leviator schematic (saved by Fritzing 0.9.3b)
breadboards: 1

parts:
  Part1 = Arduino Mega 2560 (Rev3)
  S1 = H-Bridge with L298N
  S2 = H-Bridge with L298N
  S3 = H-Bridge with L298N
  S4 = H-Bridge with L298N
  S5 = H-Bridge with L298N
  S6 = H-Bridge with L298N
  S8 = H-Bridge with L298N
  S7 = H-Bridge with L298N
  S9 = Momentary Switch [package=ksa_sealed_tac_switch]
  S10 = Momentary Switch [package=ksa_sealed_tac_switch]
  S11 = Momentary Switch [package=ksa_sealed_tac_switch]
  S12 = Momentary Switch [package=ksa_sealed_tac_switch]
  R1 = Resistor [tolerance=±5% resistance=10k package=THT]
  R2 = Resistor [tolerance=±5% resistance=10k package=THT]
  R3 = Resistor [tolerance=±5% resistance=10k package=THT]
  R4 = Resistor [tolerance=±5% resistance=10k package=THT]
  Piezo_buzzer1 = Piezo Buzzer [part_number="transducteur 1"]
  Piezo_buzzer2 = Piezo Buzzer
  Piezo_buzzer3 = Piezo Buzzer  # not connected
  Piezo_buzzer4 = Piezo Buzzer  # not connected
  Piezo_buzzer5 = Piezo Buzzer  # not connected
  Piezo_buzzer6 = Piezo Buzzer  # not connected
  Piezo_buzzer7 = Piezo Buzzer  # not connected
  Piezo_buzzer8 = Piezo Buzzer  # not connected
  Piezo_buzzer9 = Piezo Buzzer  # not connected
  Piezo_buzzer10 = Piezo Buzzer  # not connected
  Piezo_buzzer11 = Piezo Buzzer  # not connected
  Piezo_buzzer12 = Piezo Buzzer  # not connected
  Piezo_buzzer13 = Piezo Buzzer  # not connected
  Piezo_buzzer14 = Piezo Buzzer  # not connected
  Piezo_buzzer15 = Piezo Buzzer  # not connected
  Piezo_buzzer16 = Piezo Buzzer  # not connected
  Piezo_buzzer17 = Piezo Buzzer  # not connected
  Piezo_buzzer18 = Piezo Buzzer  # not connected
  Piezo_buzzer19 = Piezo Buzzer  # not connected
  Piezo_buzzer20 = Piezo Buzzer  # not connected
  Piezo_buzzer21 = Piezo Buzzer
  Piezo_buzzer22 = Piezo Buzzer  # not connected
  Piezo_buzzer23 = Piezo Buzzer  # not connected
  Piezo_buzzer24 = Piezo Buzzer  # not connected
  Piezo_buzzer25 = Piezo Buzzer  # not connected
  Piezo_buzzer26 = Piezo Buzzer  # not connected
  Piezo_buzzer27 = Piezo Buzzer  # not connected
  Piezo_buzzer28 = Piezo Buzzer  # not connected
  Piezo_buzzer29 = Piezo Buzzer  # not connected
  Piezo_buzzer30 = Piezo Buzzer
  Piezo_buzzer31 = Piezo Buzzer  # not connected
  Piezo_buzzer32 = Piezo Buzzer  # not connected
  J1 = Power Plug
  J2 = Power Jack [package=power_jack_slot]
  J4 = Power Plug
  J5 = Power Jack [package=power_jack_slot]
  J6 = Power Plug
  Piezo_buzzer33 = Piezo Buzzer  # not connected

nets:
  N1: Part1.A0, S1.IN1
  N2: Part1.A1, S1.IN2
  N3: Part1.A3, S1.IN4
  N4: Part1.5V, R1.Pin_0, R2.Pin_0, R3.Pin_0, R4.Pin_0
  N5: Part1.GND, S9.3, S10.3, S11.3, S12.3
  N6: Part1.D22, S5.IN1
  N7: Part1.D23, S5.IN2
  N8: Part1.D24, S5.IN3
  N9: Part1.D25, S5.IN4
  N10: Part1.D50, S11.2
  N11: Part1.D51, S10.2
  N12: Part1.D52, S9.2
  N13: Part1.D53, S12.2
  N14: S1.12V, J2.PWR, J2.tip_PWR, J4.PWR, J4.tip_PWR
  GND: S1.GND, S2.GND, S3.GND, S4.GND, S5.GND, S6.GND, S8.GND, S7.GND, Piezo_buzzer1.pin_1, Piezo_buzzer2.pin_1, Piezo_buzzer21.pin_2, Piezo_buzzer30.pin_1, J1.GND, J1.tip_GND, J2.GND, J2.tip_GND, J4.GND, J4.tip_GND, J5.GND, J5.tip_GND, J6.GND, J6.tip_GND
  N15: S1.5V, J1.PWR
  N16: S1.ENA, S1.ENA-5V
  N17: S1.ENB, S1.ENB-5V
  N18: S1.M1-01, Piezo_buzzer2.pin_2
  N19: S1.M1-02, Piezo_buzzer1.pin_2
  12V: S2.12V, S3.12V, S4.12V
  N20: S2.ENA, S2.ENA-5V
  N21: S2.ENB, S2.ENB-5V
  N22: S3.ENA, S3.ENA-5V
  N23: S3.ENB, S3.ENB-5V
  N24: S4.ENA, S4.ENA-5V
  N25: S4.ENB, S4.ENB-5V
  12V_2: S5.12V, S6.12V, S8.12V, S7.12V, J5.PWR, J5.tip_PWR, J6.PWR, J6.tip_PWR
  N26: S5.ENA, S5.ENA-5V
  N27: S5.ENB, S5.ENB-5V
  N28: S5.M1-01, Piezo_buzzer21.pin_1
  N29: S5.M1-02, Piezo_buzzer30.pin_2
  N30: S6.ENA, S6.ENA-5V
  N31: S6.ENB, S6.ENB-5V
  N32: S8.ENA, S8.ENA-5V
  N33: S8.ENB, S8.ENB-5V
  N34: S7.ENA, S7.ENA-5V
  N35: S7.ENB, S7.ENB-5V
  N36: S9.1, R4.Pin_1
  N37: S10.1, R3.Pin_1
  N38: S11.1, R2.Pin_1
  N39: S12.1, R1.Pin_1

notes:
  Plaque de transducteurs (Haut)
  Plaque de transducteurs (Bas)
  : Transducteurs
  Driver L298N
  Plaque de 4 drivers (bas)
  Plaque de 4 drivers (haut)
  Prise de terre de tous les
  transducteurs de la plaque du haut
  transducteurs de la plaque du bas
  Carte Arduino ATMEGA 2560
  Arrivée du courant DC 24V
  continu des 2 alimentations
  →
  ←
  : Sens d'envoi d'informations par la carte
  : Sens du courant (prise de terre)
  : Sens du courant

custom parts:
  H-Bridge with L298N: h-bridge
  Piezo Buzzer: Piezo buzzer PS1420P02CT
  Power Plug: Power Jack This is the standard 5.5mm barrel plug for power. This part has bendable leads (i.e. wires in the real world) to connect to wall warts or the breadboard in the standard wire end, and hidden connectors on the tip end that will connect when "plugged in" (overlapped with the jack so it appears "plugged in" in breadboard) to the modified coax jack part. Internal busses connect the two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
  Power Jack: Power Jack This is the standard 5.5mm barrel jack for power. Ths one is modified to mate with the barrel plug part and allow the two to "connect" so batteries and wall warts can be "connected" in breadboard and will go through to schematic.
